// Logisim project nand2tetris.circ as structural Verilog
module Not (
  input  Input,
  output Output
);

  nand nand_1 (Output, Input, Input);
endmodule

module And (
  input  in_1,
  input  in_2,
  output out_3
);

  wire nand_1_out;

  nand nand_1 (nand_1_out, in_1, in_2);
  Not not_1 (.Input(nand_1_out), .Output(out_3));
endmodule

module Or (
  input  a,
  input  b,
  output out_3
);

  wire not_1_output, not_2_output;

  Not not_1 (.Input(a), .Output(not_1_output));
  Not not_2 (.Input(b), .Output(not_2_output));
  nand nand_1 (out_3, not_1_output, not_2_output);
endmodule

module Xor (
  input  a,
  input  b,
  output out_3
);

  wire nand_1_out, nand_2_out, not_1_output, not_2_output;

  Not not_1 (.Input(a), .Output(not_1_output));
  Not not_2 (.Input(b), .Output(not_2_output));
  nand nand_1 (nand_1_out, not_1_output, b);
  nand nand_2 (nand_2_out, a, not_2_output);
  nand nand_3 (out_3, nand_1_out, nand_2_out);
endmodule

module Mux (
  input  sel,
  input  a,
  input  b,
  output out
);

  wire and_1_out_3, and_2_out_3, not_1_output;

  Not not_1 (.Input(sel), .Output(not_1_output));
  And and_1 (.in_1(not_1_output), .in_2(a), .out_3(and_1_out_3));
  And and_2 (.in_1(sel), .in_2(b), .out_3(and_2_out_3));
  Or or_1 (.a(and_1_out_3), .b(and_2_out_3), .out_3(out));
endmodule

module Dmux (
  input  sel,
  input  in,
  output a,
  output b
);

  wire not_1_output;

  Not not_1 (.Input(sel), .Output(not_1_output));
  And and_1 (.in_1(not_1_output), .in_2(in), .out_3(a));
  And and_2 (.in_1(sel), .in_2(in), .out_3(b));

  // Notes on the sheet:
  //   if(sel) a = in b = 0
  //   if(!sel) a = 0 b = in
endmodule

module Not16 (
  input  [15:0] in16,
  output [15:0] out16
);

  Not not_1 (.Input(in16[0]), .Output(out16[0]));
  Not not_2 (.Input(in16[1]), .Output(out16[1]));
  Not not_3 (.Input(in16[2]), .Output(out16[2]));
  Not not_4 (.Input(in16[3]), .Output(out16[3]));
  Not not_5 (.Input(in16[4]), .Output(out16[4]));
  Not not_6 (.Input(in16[5]), .Output(out16[5]));
  Not not_7 (.Input(in16[6]), .Output(out16[6]));
  Not not_8 (.Input(in16[7]), .Output(out16[7]));
  Not not_9 (.Input(in16[8]), .Output(out16[8]));
  Not not_10 (.Input(in16[9]), .Output(out16[9]));
  Not not_11 (.Input(in16[10]), .Output(out16[10]));
  Not not_12 (.Input(in16[11]), .Output(out16[11]));
  Not not_13 (.Input(in16[12]), .Output(out16[12]));
  Not not_14 (.Input(in16[13]), .Output(out16[13]));
  Not not_15 (.Input(in16[14]), .Output(out16[14]));
  Not not_16 (.Input(in16[15]), .Output(out16[15]));
endmodule

module And16 (
  input  [15:0] a16,
  input  [15:0] b16,
  output [15:0] out16
);

  And and_1 (.in_1(a16[0]), .in_2(b16[0]), .out_3(out16[0]));
  And and_2 (.in_1(a16[1]), .in_2(b16[1]), .out_3(out16[1]));
  And and_3 (.in_1(a16[2]), .in_2(b16[2]), .out_3(out16[2]));
  And and_4 (.in_1(a16[3]), .in_2(b16[3]), .out_3(out16[3]));
  And and_5 (.in_1(a16[4]), .in_2(b16[4]), .out_3(out16[4]));
  And and_6 (.in_1(a16[5]), .in_2(b16[5]), .out_3(out16[5]));
  And and_7 (.in_1(a16[6]), .in_2(b16[6]), .out_3(out16[6]));
  And and_8 (.in_1(a16[7]), .in_2(b16[7]), .out_3(out16[7]));
  And and_9 (.in_1(a16[8]), .in_2(b16[8]), .out_3(out16[8]));
  And and_10 (.in_1(a16[9]), .in_2(b16[9]), .out_3(out16[9]));
  And and_11 (.in_1(a16[10]), .in_2(b16[10]), .out_3(out16[10]));
  And and_12 (.in_1(a16[11]), .in_2(b16[11]), .out_3(out16[11]));
  And and_13 (.in_1(a16[12]), .in_2(b16[12]), .out_3(out16[12]));
  And and_14 (.in_1(a16[13]), .in_2(b16[13]), .out_3(out16[13]));
  And and_15 (.in_1(a16[14]), .in_2(b16[14]), .out_3(out16[14]));
  And and_16 (.in_1(a16[15]), .in_2(b16[15]), .out_3(out16[15]));
endmodule

module Or16 (
  input  [15:0] in_1,
  input  [15:0] in_2,
  output [15:0] out_3
);

  Or or_1 (.a(in_1[0]), .b(in_2[0]), .out_3(out_3[0]));
  Or or_2 (.a(in_1[1]), .b(in_2[1]), .out_3(out_3[1]));
  Or or_3 (.a(in_1[2]), .b(in_2[2]), .out_3(out_3[2]));
  Or or_4 (.a(in_1[3]), .b(in_2[3]), .out_3(out_3[3]));
  Or or_5 (.a(in_1[4]), .b(in_2[4]), .out_3(out_3[4]));
  Or or_6 (.a(in_1[5]), .b(in_2[5]), .out_3(out_3[5]));
  Or or_7 (.a(in_1[6]), .b(in_2[6]), .out_3(out_3[6]));
  Or or_8 (.a(in_1[7]), .b(in_2[7]), .out_3(out_3[7]));
  Or or_9 (.a(in_1[8]), .b(in_2[8]), .out_3(out_3[8]));
  Or or_10 (.a(in_1[9]), .b(in_2[9]), .out_3(out_3[9]));
  Or or_11 (.a(in_1[10]), .b(in_2[10]), .out_3(out_3[10]));
  Or or_12 (.a(in_1[11]), .b(in_2[11]), .out_3(out_3[11]));
  Or or_13 (.a(in_1[12]), .b(in_2[12]), .out_3(out_3[12]));
  Or or_14 (.a(in_1[13]), .b(in_2[13]), .out_3(out_3[13]));
  Or or_15 (.a(in_1[14]), .b(in_2[14]), .out_3(out_3[14]));
  Or or_16 (.a(in_1[15]), .b(in_2[15]), .out_3(out_3[15]));
endmodule

module Mux16 (
  input  [15:0] a16,
  input  sel,
  input  [15:0] b16,
  output [15:0] out16
);

  Mux mux_1 (.sel(sel), .a(a16[0]), .b(b16[0]), .out(out16[0]));
  Mux mux_2 (.sel(sel), .a(a16[1]), .b(b16[1]), .out(out16[1]));
  Mux mux_3 (.sel(sel), .a(a16[2]), .b(b16[2]), .out(out16[2]));
  Mux mux_4 (.sel(sel), .a(a16[3]), .b(b16[3]), .out(out16[3]));
  Mux mux_5 (.sel(sel), .a(a16[4]), .b(b16[4]), .out(out16[4]));
  Mux mux_6 (.sel(sel), .a(a16[5]), .b(b16[5]), .out(out16[5]));
  Mux mux_7 (.sel(sel), .a(a16[6]), .b(b16[6]), .out(out16[6]));
  Mux mux_8 (.sel(sel), .a(a16[7]), .b(b16[7]), .out(out16[7]));
  Mux mux_9 (.sel(sel), .a(a16[8]), .b(b16[8]), .out(out16[8]));
  Mux mux_10 (.sel(sel), .a(a16[9]), .b(b16[9]), .out(out16[9]));
  Mux mux_11 (.sel(sel), .a(a16[10]), .b(b16[10]), .out(out16[10]));
  Mux mux_12 (.sel(sel), .a(a16[11]), .b(b16[11]), .out(out16[11]));
  Mux mux_13 (.sel(sel), .a(a16[12]), .b(b16[12]), .out(out16[12]));
  Mux mux_14 (.sel(sel), .a(a16[13]), .b(b16[13]), .out(out16[13]));
  Mux mux_15 (.sel(sel), .a(a16[14]), .b(b16[14]), .out(out16[14]));
  Mux mux_16 (.sel(sel), .a(a16[15]), .b(b16[15]), .out(out16[15]));
endmodule

module Or8Way (
  input  [7:0] in8,
  output out
);

  wire or_1_out_3, or_2_out_3, or_3_out_3, or_4_out_3, or_5_out_3, or_6_out_3;

  Or or_1 (.a(in8[0]), .b(in8[1]), .out_3(or_1_out_3));
  Or or_2 (.a(or_1_out_3), .b(in8[2]), .out_3(or_2_out_3));
  Or or_3 (.a(or_2_out_3), .b(in8[3]), .out_3(or_3_out_3));
  Or or_4 (.a(or_3_out_3), .b(in8[4]), .out_3(or_4_out_3));
  Or or_5 (.a(or_4_out_3), .b(in8[5]), .out_3(or_5_out_3));
  Or or_6 (.a(or_5_out_3), .b(in8[6]), .out_3(or_6_out_3));
  Or or_7 (.a(or_6_out_3), .b(in8[7]), .out_3(out));
endmodule

module Mux4Way16 (
  input  [1:0] sel2,
  input  [15:0] a16,
  input  [15:0] b16,
  input  [15:0] c16,
  input  [15:0] d16,
  output [15:0] out16
);

  wire [15:0] mux16_1_out16, mux16_2_out16;

  Mux16 mux16_1 (.a16(a16), .out16(mux16_1_out16), .b16(b16), .sel(sel2[0]));
  Mux16 mux16_2 (.a16(c16), .out16(mux16_2_out16), .b16(d16), .sel(sel2[0]));
  Mux16 mux16_3 (.a16(mux16_1_out16), .out16(out16), .b16(mux16_2_out16), .sel(sel2[1]));
endmodule

module Mux8Way16 (
  input  [2:0] sel3,
  input  [15:0] a16,
  input  [15:0] b16,
  input  [15:0] c16,
  input  [15:0] d16,
  input  [15:0] e16,
  input  [15:0] f16,
  input  [15:0] g16,
  input  [15:0] h16,
  output [15:0] out16
);

  wire [15:0] mux4way16_1_out16, mux4way16_2_out16;

  Mux4Way16 mux4way16_1 (.sel2(sel3[1:0]), .a16(a16), .b16(b16), .c16(c16), .d16(d16), .out16(mux4way16_1_out16));
  Mux4Way16 mux4way16_2 (.sel2(sel3[1:0]), .a16(e16), .b16(f16), .c16(g16), .d16(h16), .out16(mux4way16_2_out16));
  Mux16 mux16_1 (.a16(mux4way16_1_out16), .out16(out16), .b16(mux4way16_2_out16), .sel(sel3[2]));
endmodule

module DMux4Way (
  input  [1:0] sel2,
  input  in,
  output a,
  output b,
  output c,
  output d
);

  wire dmux_1_a, dmux_1_b;

  Dmux dmux_1 (.sel(sel2[1]), .in(in), .a(dmux_1_a), .b(dmux_1_b));
  Dmux dmux_2 (.sel(sel2[0]), .in(dmux_1_a), .a(a), .b(b));
  Dmux dmux_3 (.sel(sel2[0]), .in(dmux_1_b), .a(c), .b(d));
endmodule

module DMux8Way (
  input  [2:0] sel3,
  input  in,
  output a,
  output b,
  output c,
  output d,
  output e,
  output f,
  output g,
  output h
);

  wire dmux4way_1_a, dmux4way_1_b, dmux4way_1_c, dmux4way_1_d;

  DMux4Way dmux4way_1 (
    .sel2(sel3[2:1]), .in(in), .a(dmux4way_1_a), .b(dmux4way_1_b), .c(dmux4way_1_c), .d(dmux4way_1_d));
  Dmux dmux_1 (.sel(sel3[0]), .in(dmux4way_1_a), .a(a), .b(b));
  Dmux dmux_2 (.sel(sel3[0]), .in(dmux4way_1_b), .a(c), .b(d));
  Dmux dmux_3 (.sel(sel3[0]), .in(dmux4way_1_c), .a(e), .b(f));
  Dmux dmux_4 (.sel(sel3[0]), .in(dmux4way_1_d), .a(g), .b(h));
endmodule

module HalfAdder (
  input  a,
  input  b,
  output sum,
  output carry
);

  Xor xor_1 (.a(a), .b(b), .out_3(sum));
  And and_1 (.in_1(a), .in_2(b), .out_3(carry));
endmodule

module FullAdder (
  input  a,
  input  b,
  input  c,
  output sum,
  output carry
);

  wire halfadder_1_carry, halfadder_1_sum, halfadder_2_carry;

  HalfAdder halfadder_1 (.a(a), .b(b), .sum(halfadder_1_sum), .carry(halfadder_1_carry));
  HalfAdder halfadder_2 (.a(halfadder_1_sum), .b(c), .sum(sum), .carry(halfadder_2_carry));
  Or or_1 (.a(halfadder_2_carry), .b(halfadder_1_carry), .out_3(carry));
endmodule

module Add16 (
  input  [15:0] a16,
  input  [15:0] b16,
  output [15:0] out16
);

  wire fulladder_1_carry, fulladder_2_carry, fulladder_3_carry, fulladder_4_carry, fulladder_5_carry,
       fulladder_6_carry, fulladder_7_carry, fulladder_8_carry, fulladder_9_carry, fulladder_10_carry,
       fulladder_11_carry, fulladder_12_carry, fulladder_13_carry, fulladder_14_carry, halfadder_1_carry;

  HalfAdder halfadder_1 (.a(a16[0]), .b(b16[0]), .sum(out16[0]), .carry(halfadder_1_carry));
  FullAdder fulladder_1 (.a(a16[1]), .b(b16[1]), .c(halfadder_1_carry), .sum(out16[1]), .carry(fulladder_1_carry));
  FullAdder fulladder_2 (.a(a16[2]), .b(b16[2]), .c(fulladder_1_carry), .sum(out16[2]), .carry(fulladder_2_carry));
  FullAdder fulladder_3 (.a(a16[3]), .b(b16[3]), .c(fulladder_2_carry), .sum(out16[3]), .carry(fulladder_3_carry));
  FullAdder fulladder_4 (.a(a16[4]), .b(b16[4]), .c(fulladder_3_carry), .sum(out16[4]), .carry(fulladder_4_carry));
  FullAdder fulladder_5 (.a(a16[5]), .b(b16[5]), .c(fulladder_4_carry), .sum(out16[5]), .carry(fulladder_5_carry));
  FullAdder fulladder_6 (.a(a16[6]), .b(b16[6]), .c(fulladder_5_carry), .sum(out16[6]), .carry(fulladder_6_carry));
  FullAdder fulladder_7 (.a(a16[7]), .b(b16[7]), .c(fulladder_6_carry), .sum(out16[7]), .carry(fulladder_7_carry));
  FullAdder fulladder_8 (.a(a16[8]), .b(b16[8]), .c(fulladder_7_carry), .sum(out16[8]), .carry(fulladder_8_carry));
  FullAdder fulladder_9 (.a(a16[9]), .b(b16[9]), .c(fulladder_8_carry), .sum(out16[9]), .carry(fulladder_9_carry));
  FullAdder fulladder_10 (.a(a16[10]), .b(b16[10]), .c(fulladder_9_carry), .sum(out16[10]), .carry(fulladder_10_carry));
  FullAdder fulladder_11 (
    .a(a16[11]), .b(b16[11]), .c(fulladder_10_carry), .sum(out16[11]), .carry(fulladder_11_carry));
  FullAdder fulladder_12 (
    .a(a16[12]), .b(b16[12]), .c(fulladder_11_carry), .sum(out16[12]), .carry(fulladder_12_carry));
  FullAdder fulladder_13 (
    .a(a16[13]), .b(b16[13]), .c(fulladder_12_carry), .sum(out16[13]), .carry(fulladder_13_carry));
  FullAdder fulladder_14 (
    .a(a16[14]), .b(b16[14]), .c(fulladder_13_carry), .sum(out16[14]), .carry(fulladder_14_carry));
  FullAdder fulladder_15 (.a(a16[15]), .b(b16[15]), .c(fulladder_14_carry), .sum(out16[15]));  // open: carry
endmodule

module Inc16 (
  input  [15:0] in16,
  output [15:0] out16
);

  Add16 add16_1 (.a16(in16), .b16(16'h1), .out16(out16));
endmodule

module ALU (
  input  zx,
  input  nx,
  input  zy,
  input  ny,
  input  f,
  input  no,
  input  [15:0] x16,
  input  [15:0] y16,
  output [15:0] out16,
  output zr,
  output ng
);

  wire not_1_output, not_2_output, or8way_1_out, or8way_2_out;
  wire [15:0] add16_1_out16, and16_1_out16, mux16_1_out16, mux16_2_out16, mux16_3_out16, mux16_4_out16,
       mux16_5_out16, not16_1_out16, not16_2_out16, not16_3_out16;

  Mux16 mux16_1 (.a16(x16), .out16(mux16_1_out16), .b16({16{1'b0}}), .sel(zx));
  Not16 not16_1 (.in16(mux16_1_out16), .out16(not16_1_out16));
  Mux16 mux16_2 (.a16(mux16_1_out16), .out16(mux16_2_out16), .b16(not16_1_out16), .sel(nx));
  Mux16 mux16_3 (.a16(y16), .out16(mux16_3_out16), .b16({16{1'b0}}), .sel(zy));
  Not16 not16_2 (.in16(mux16_3_out16), .out16(not16_2_out16));
  Mux16 mux16_4 (.a16(mux16_3_out16), .out16(mux16_4_out16), .b16(not16_2_out16), .sel(ny));
  Add16 add16_1 (.a16(mux16_2_out16), .b16(mux16_4_out16), .out16(add16_1_out16));
  And16 and16_1 (.a16(mux16_2_out16), .b16(mux16_4_out16), .out16(and16_1_out16));
  Mux16 mux16_5 (.a16(and16_1_out16), .out16(mux16_5_out16), .b16(add16_1_out16), .sel(f));
  Not16 not16_3 (.in16(mux16_5_out16), .out16(not16_3_out16));
  Mux16 mux16_6 (.a16(mux16_5_out16), .out16({ng, out16[14:0]}), .b16(not16_3_out16), .sel(no));
  Or8Way or8way_1 (.in8(out16[7:0]), .out(or8way_1_out));
  Or8Way or8way_2 (.in8({ng, out16[14:8]}), .out(or8way_2_out));
  Not not_1 (.Input(or8way_1_out), .Output(not_1_output));
  Not not_2 (.Input(or8way_2_out), .Output(not_2_output));
  And and_1 (.in_1(not_1_output), .in_2(not_2_output), .out_3(zr));

  assign out16[15] = ng;
endmodule
